# Fritzing sketch heatingController (saved by Fritzing 0.9.3b)
breadboards: 1

parts:
  Součástka1 = Arduino Uno (Rev3)
  S1 = Pushbutton [package="[THT]"]
  S2 = Pushbutton [package="[THT]"]
  S3 = Pushbutton [package="[THT]"]
  R1 = Resistor [tolerance=±5% resistance=10k package=THT]
  R2 = Resistor [tolerance=±5% resistance=10k package=THT]
  R3 = Resistor [tolerance=±5% resistance=10k package=THT]

nets:
  N1: Součástka1.GND, R1.Pin_1, R2.Pin_1, R3.Pin_1
  N2: Součástka1.D2, S3.Pin_3, S3.Pin_4, R3.Pin_0
  N3: Součástka1.D3_PWM, S2.Pin_3, S2.Pin_4, R2.Pin_0
  N4: Součástka1.D4, S1.Pin_3, S1.Pin_4, R1.Pin_0
  N5: Součástka1.5V, S1.Pin_1, S1.Pin_2, S2.Pin_1, S2.Pin_2, S3.Pin_1, S3.Pin_2

// code stored in the sketch: heatingController.ino

